# Fritzing sketch NapkinFire (saved by Fritzing 0.9.3b)
circuit board: 6.25cm x 6.25cm
breadboards: 1

parts:
  LOUD = Piezo Speaker [part_number=" COM-13940"]
  PIR = PIR sensor
  J1 = double row female pin header, 16 pins [form="♀ (female)"]
  J2 = double row female pin header, 16 pins [form="♀ (female)"]
  J3 = double row female pin header, 16 pins [form="♀ (female)"]
  J4 = double row female pin header, 16 pins [form="♀ (female)"]
  ^Arducam = Arducam [package=THT]
  JMPR = Resistor [tolerance=±5% resistance=220 package="0805 [SMD]"]
  microSD1 = MicroSD Breakout
  <NeoPix = Neopixel Strip -- Black (30/m)
  IR = female pin header, 6 pins [form="♀ (female)"]
  ESP32_Feather = Adafruit HUZZAH32 ESP32 Feather [part_number="Adafruit #3405"]
  J5 = Audio Plug [package=THT]

nets:
  GND: LOUD.pin1, PIR.GND, J1.pin1, J1.pin2, J1.pin3, J1.pin4, J1.pin5, J1.pin6, J1.pin7, J1.pin8, J1.pin9, J1.pin10, J1.pin11, J1.pin12, J1.pin13, J1.pin14, J1.pin15, J1.pin16, J2.pin1, J2.pin2, J2.pin3, J2.pin4, J2.pin5, J2.pin6, J2.pin7, J2.pin8, J2.pin9, J2.pin10, J2.pin11, J2.pin12, J2.pin13, J2.pin14, J2.pin15, J2.pin16, J3.pin1, J3.pin2, J3.pin3, J3.pin4, J3.pin5, J3.pin6, J3.pin7, J3.pin8, J3.pin9, J3.pin10, J3.pin11, J3.pin12, J3.pin13, J3.pin14, J3.pin15, J3.pin16, J4.pin1, J4.pin2, J4.pin3, J4.pin4, J4.pin5, J4.pin6, J4.pin7, J4.pin8, J4.pin9, J4.pin10, J4.pin11, J4.pin12, J4.pin13, J4.pin14, J4.pin15, J4.pin16, ^Arducam.GND, JMPR.Pin_1, microSD1.GND, <NeoPix.GND, ESP32_Feather.IO21, ESP32_Feather.IO17, ESP32_Feather.IO16, J5.pin1
  N1: LOUD.pin2, ESP32_Feather.IO32_A7
  VDD: PIR.VDD, ^Arducam.VCC, JMPR.Pin_0, microSD1.3v, <NeoPix.+5V, ESP32_Feather.3.3V
  N2: PIR.SIG, ESP32_Feather.IO27_A10
  N3: ^Arducam.CS, ESP32_Feather.IO14_A6
  N4: ^Arducam.MOSI, microSD1.DO, ESP32_Feather.MOSI
  N5: ^Arducam.MISO, microSD1.DI, ESP32_Feather.MISO
  N6: ^Arducam.SCK, microSD1.CLK, ESP32_Feather.SCK
  N7: ^Arducam.SDA, ESP32_Feather.SDA
  N8: ^Arducam.SCL, ESP32_Feather.SCL
  N9: microSD1.CS, ESP32_Feather.IO13_A12
  N10: <NeoPix.Din, ESP32_Feather.A5_IO4
  N11: IR.pin1, IR.pin2, IR.pin3, ESP32_Feather.GND
  N12: IR.pin4, ESP32_Feather.A0_DAC2
  N13: IR.pin5, ESP32_Feather.A1_DAC1
  N14: IR.pin6, ESP32_Feather.A4_IO36
  N15: ESP32_Feather.IO15_A8, J5.pin2, J5.pin3

notes:
  3V
  0V
  IO1
  IO2
  IO3
  CS
  DI
  DO
  CLK
  GND
  SIG
  NeoPix
  MOSI
  MISO
  SDA
  SCL
  R
  L

custom parts:
  Arducam: A Arducam moudle
  MicroSD Breakout: 5V-ready microSD Breakout with Level Shifter
  Neopixel Strip -- Black (30/m): These NeoPixel strips have 30 digitally-addressable pixel LEDs per meter and are very affordable and are only 12.5 mm wide, 10 mm if you remove the strip from the casing.
  Audio Plug: Adafruit audio plug
